// Logisim project main_page.circ as structural Verilog: 4 circuits, main circuit control_unit
module main (
  output [3:0] out_1,
  output [7:0] out_2,
  output [3:0] out_3,
  output [7:0] out_4,
  output [7:0] out_5,
  output [7:0] out_6
);

  wire button_1_out, clock_1_out, control_unit_1_memw, control_unit_1_pcsrc, control_unit_1_rasrc,
       control_unit_1_regsrc, control_unit_1_regw, control_unit_1_ulasrc, ula_1_zero;
  wire [7:0] memoria_dout, multiplexer_2_out, ula_1_ula_result;
  wire [23:0] adder_1_out, adder_2_out, bit_extender_1_out, multiplexer_1_out, register_1_q;

  Multiplexer #(.width(24)) multiplexer_1 (
    .in0(adder_2_out), .in1(adder_1_out), .out(multiplexer_1_out), .sel(control_unit_1_pcsrc));
  Register #(.width(24)) register_1 (
    .D(multiplexer_1_out), .en(1'b1), .clk(clock_1_out), .Q(register_1_q), .clr(button_1_out));
  Clock clock_1 (.out(clock_1_out));
  Button button_1 (.out(button_1_out));
  ROM #(.addrWidth(24)) instructions (.addr(register_1_q), .data({out_1, out_2[3:0]}));
  Adder #(.width(24)) adder_1 (.a(adder_2_out), .b(bit_extender_1_out), .out(adder_1_out), .cin(1'b0));  // open: cout
  Adder #(.width(24)) adder_2 (.a(register_1_q), .b(24'h1), .out(adder_2_out), .cin(1'b0));  // open: cout
  assign bit_extender_1_out = {{16{multiplexer_2_out[7]}}, multiplexer_2_out};  // Bit_Extender bit_extender_1
  control_unit control_unit_1 (
    .instruction(out_1), .zero(ula_1_zero), .RegW(control_unit_1_regw), .ULASrc(control_unit_1_ulasrc),
    .ULAOp(out_3), .MemW(control_unit_1_memw), .RegSrc(control_unit_1_regsrc), .PcSrc(control_unit_1_pcsrc),
    .raSrc(control_unit_1_rasrc));  // open: B, J
  registers registers_1 (
    .data(out_6), .write(control_unit_1_regw), .clock(clock_1_out), .b(out_2[3:2]), .a(out_2[1:0]),
    .reset(button_1_out), .endereco(out_2[1:0]), .regaSrc(control_unit_1_rasrc), .ra(out_4), .rb(out_5));
  Multiplexer #(.width(8)) multiplexer_2 (
    .in0(out_5), .in1({4'b0000, out_2[3:0]}), .out(multiplexer_2_out), .sel(control_unit_1_ulasrc));
  RAM memoria (
    .addr(ula_1_ula_result), .we(control_unit_1_memw), .oe(1'b1), .clk(clock_1_out), .din(out_5),
    .dout(memoria_dout));
  ula ula_1 (.ra(out_4), .rb(multiplexer_2_out), .ula_src(out_3), .zero(ula_1_zero), .ula_result(ula_1_ula_result));
  Multiplexer #(.width(8)) multiplexer_3 (
    .in0(ula_1_ula_result), .in1(memoria_dout), .out(out_6), .sel(control_unit_1_regsrc));

  assign out_2[7:4] = out_1;

  // Notes on the sheet:
  //   contents of instructions (hex, n*v repeats v):
  //   88 1 91 54 b1
endmodule

module control_unit (
  input  [3:0] instruction,
  input  zero,
  output RegW,
  output ULASrc,
  output [3:0] ULAOp,
  output MemW,
  output RegSrc,
  output B,
  output PcSrc,
  output J,
  output raSrc
);

  wire and_1_out;
  wire [15:11] control_unit_data;

  ROM #(.addrWidth(4), .dataWidth(16)) control_unit (
    .addr(instruction), .data({control_unit_data, RegW, ULASrc, ULAOp, MemW, RegSrc, B, J, raSrc}));
  and and_1 (and_1_out, B, zero);
  or or_1 (PcSrc, and_1_out, J);

  // Notes on the sheet:
  //   contents of control_unit (hex, n*v repeats v):
  //   24 520 2 202 408 10 500 6e1 6c1 400 420 460 480 440 4a0 520
endmodule

module registers (
  input  [7:0] data,
  input  write,
  input  clock,
  input  [1:0] b,
  input  [1:0] a,
  input  reset,
  input  [1:0] endereco,
  input  regaSrc,
  output [7:0] ra,
  output [7:0] rb
);

  wire and_1_out, decoder_1_out0, decoder_1_out1, decoder_1_out2, decoder_1_out3;
  wire [1:0] multiplexer_3_out;
  wire [7:0] register_1_q, register_2_q, register_3_q, register_4_q;

  and and_1 (and_1_out, write, clock);
  Decoder #(.enable("false"), .select(2)) decoder_1 (
    .out0(decoder_1_out0), .out1(decoder_1_out1), .out2(decoder_1_out2), .out3(decoder_1_out3), .sel(endereco));
  Register register_1 (.D(data), .en(decoder_1_out0), .clk(and_1_out), .Q(register_1_q), .clr(reset));
  Register register_2 (.D(data), .en(decoder_1_out1), .clk(and_1_out), .Q(register_2_q), .clr(reset));
  Register register_3 (.D(data), .en(decoder_1_out2), .clk(and_1_out), .Q(register_3_q), .clr(reset));
  Register register_4 (.D(data), .en(decoder_1_out3), .clk(and_1_out), .Q(register_4_q), .clr(reset));
  Multiplexer #(.select(2), .width(8)) multiplexer_1 (
    .in0(register_1_q), .in1(register_2_q), .in2(register_3_q), .in3(register_4_q), .out(ra),
    .sel(multiplexer_3_out));
  Multiplexer #(.select(2), .width(8)) multiplexer_2 (
    .in0(register_1_q), .in1(register_2_q), .in2(register_3_q), .in3(register_4_q), .out(rb), .sel(b));
  Multiplexer #(.width(2)) multiplexer_3 (.in0(a), .in1(2'b00), .out(multiplexer_3_out), .sel(regaSrc));
endmodule

module ula (
  input  [7:0] ra,
  input  [7:0] rb,
  input  [3:0] ula_src,
  output zero,
  output [7:0] ula_result
);

  wire and_2_out, and_3_out, nor_1_out, nor_2_out, nor_3_out, nor_4_out;
  wire [7:0] adder_1_out, and_1_out, not_1_out, or_1_out, shifter_1_out, shifter_2_out, subtractor_1_out;

  Adder adder_1 (.a(ra), .b(rb), .out(adder_1_out), .cin(1'b0));  // open: cout
  Subtractor subtractor_1 (.a(ra), .b(rb), .out(subtractor_1_out), .bin(1'b0));  // open: bout
  assign not_1_out = ~rb;  // NOT_Gate not_1, 8 bits wide
  assign and_1_out = ra & rb;  // AND_Gate and_1, 8 bits wide
  assign or_1_out = ra | rb;  // OR_Gate or_1, 8 bits wide
  Shifter shifter_1 (.in(ra), .\dist (rb[2:0]), .out(shifter_1_out));
  Shifter #(.shift("lr")) shifter_2 (.in(ra), .\dist (rb[2:0]), .out(shifter_2_out));
  Multiplexer #(.select(4), .width(8)) multiplexer_1 (
    .in0(adder_1_out), .in1(subtractor_1_out), .in2(not_1_out), .in3(and_1_out), .in4(or_1_out),
    .in5(shifter_1_out), .in6({ra[3:0], rb[3:0]}), .in7({rb[3:0], ra[7:4]}), .in8(rb), .in9(shifter_2_out),
    .in10({8{1'b0}}), .in11({8{1'b0}}), .in12({8{1'b0}}), .in13({8{1'b0}}), .in14({8{1'b0}}),
    .in15({8{1'b0}}), .out(ula_result), .sel(ula_src));
  nor nor_1 (nor_1_out, ra[0], ra[1]);
  and and_2 (and_2_out, nor_1_out, nor_2_out);
  nor nor_2 (nor_2_out, ra[2], ra[3]);
  nor nor_3 (nor_3_out, ra[4], ra[5]);
  and and_3 (and_3_out, nor_3_out, nor_4_out);
  nor nor_4 (nor_4_out, ra[6], ra[7]);
  and and_4 (zero, and_2_out, and_3_out);
endmodule
